// Logisim project trabfinal.circ as structural Verilog: 10 circuits, main circuit display
// bl
module main (
  input  [3:0] A,
  input  [3:0] B,
  input  [3:0] in_3,
  input  [3:0] C,
  input  [3:0] in_5,
  input  [3:0] D,
  input  [1:0] ENTRADA_1,
  input  in_8,
  input  [1:0] ENTRADA_2,
  input  SOMA___0,
  input  in_11,
  input  in_12,
  input  in_13,
  input  in_14,
  input  in_15,
  input  in_16,
  input  [1:0] in_17,
  input  in_18,
  input  in_19,
  input  [3:0] in_20,
  input  in_21,
  input  [3:0] in_22,
  input  [3:0] in_23,
  input  [3:0] in_24,
  input  in_25,
  output [3:0] out_26,
  output out_27,
  output out_28,
  output [3:0] out_29,
  output [3:0] out_30
);

  wire adder_1_cout, displaytwo_1_a_2, displaytwo_1_b_2, displaytwo_1_c_2, displaytwo_1_d_2, displaytwo_1_e,
       displaytwo_1_f, displaytwo_1_g, displaytwo_1_ponto, select2two_1_out_5, select2two_2_out_5,
       select_1_out_10;
  wire [3:0] select2two_2_out, select_1_out_8, select_1_out_9;

  select select_1 (
    .in_1(A), .in_2(B), .in_3(C), .in_4(D), .in_5(ENTRADA_1), .in_6(ENTRADA_2), .in_7(SOMA___0),
    .out_8(select_1_out_8), .out_9(select_1_out_9), .out_10(select_1_out_10));
  select2two select2two_1 (
    .A(select_1_out_8), .B(select_1_out_9), .in_3(select_1_out_10), .OUT(out_26), .out_5(select2two_1_out_5));
  LED led_1 (.in(select2two_1_out_5));
  select2two select2two_2 (.A(in_3), .B(in_5), .in_3(in_8), .OUT(select2two_2_out), .out_5(select2two_2_out_5));
  LED led_2 (.in(select2two_2_out_5));
  displayTwo displaytwo_1 (
    .A(select2two_2_out[3]), .B(select2two_2_out[2]), .C(select2two_2_out[1]), .D(select2two_2_out[0]),
    .a_2(displaytwo_1_a_2), .b_2(displaytwo_1_b_2), .c_2(displaytwo_1_c_2), .d_2(displaytwo_1_d_2),
    .e(displaytwo_1_e), .f(displaytwo_1_f), .g(displaytwo_1_g), .ponto(displaytwo_1_ponto));
  _7_Segment_Display u_7_segment_display_1 (
    .g(displaytwo_1_g), .f(displaytwo_1_f), .a(displaytwo_1_a_2), .b(displaytwo_1_b_2), .e(displaytwo_1_e),
    .d(displaytwo_1_d_2), .c(displaytwo_1_c_2), .dp(displaytwo_1_ponto));
  Multiplexer multiplexer_1 (.in0(in_16), .in1(in_18), .out(out_28), .sel(in_21), .en(in_19));
  Subtractor #(.width(4)) subtractor_1 (.a(in_20), .b(in_22), .out(out_29));  // open: bin, bout
  Adder #(.width(4)) adder_1 (.a(in_23), .b(in_24), .out(out_30), .cin(in_25), .cout(adder_1_cout));
  LED led_3 (.in(adder_1_cout));
  Multiplexer #(.select(2)) multiplexer_2 (
    .in0(in_14), .in1(in_13), .in2(in_12), .in3(in_11), .out(out_27), .sel(in_17), .en(in_15));

  // Notes on the sheet:
  //   Trabalho Final 
  //   SUBTRACAO = 1
  //   00 = A
  //   01 = B
  //   10 = C
  //   11 = D
  //   out 1
  //   out 2
  //   2 + 2 = 4
  //   9 + 1 = 10
  //   15 + 2 = 17
  //   3 - 1 = 2
  //   1 - 3 = -2
  //   15 - 2 = 13 > 10
  //   -> 16 + Número do display
  //   0 = soma
  //   1 = subtração
  //   aqui eu seleciona qual entrada usara
endmodule

module display (
  input  A,
  input  B,
  input  C,
  input  D,
  output a_2,
  output b_2,
  output c_2,
  output d_2,
  output e,
  output f,
  output g
);

  wire and_1_out, and_2_out, and_3_out, and_4_out, and_5_out, and_6_out, and_7_out, and_8_out, and_9_out,
       and_10_out, and_11_out, and_12_out, and_13_out, and_14_out, and_15_out, and_16_out, not_1_out,
       not_2_out, not_3_out, not_4_out, not_5_out, not_6_out, not_7_out, not_8_out, not_9_out, not_10_out,
       not_11_out, not_12_out, not_13_out, not_14_out, not_15_out, not_16_out, not_17_out, not_18_out,
       not_19_out, not_20_out, not_21_out;

  not not_1 (not_1_out, B);
  and and_1 (and_1_out, not_1_out, not_2_out);
  not not_2 (not_2_out, D);
  and and_2 (and_2_out, B, D);
  not not_3 (not_3_out, B);
  not not_4 (not_4_out, C);
  and and_3 (and_3_out, not_4_out, not_5_out);
  not not_5 (not_5_out, D);
  and and_4 (and_4_out, C, D);
  not not_6 (not_6_out, C);
  or or_1 (c_2, not_6_out, D, B);
  not not_7 (not_7_out, B);
  and and_5 (and_5_out, not_7_out, not_8_out);
  not not_8 (not_8_out, D);
  not not_9 (not_9_out, B);
  and and_6 (and_6_out, not_9_out, C);
  and and_7 (and_7_out, C, not_10_out);
  not not_10 (not_10_out, D);
  not not_11 (not_11_out, C);
  and and_8 (and_8_out, B, not_11_out, D);
  not not_12 (not_12_out, B);
  and and_9 (and_9_out, not_12_out, not_13_out);
  not not_13 (not_13_out, D);
  and and_10 (and_10_out, C, not_14_out);
  not not_14 (not_14_out, D);
  not not_15 (not_15_out, C);
  and and_11 (and_11_out, not_15_out, not_16_out);
  not not_16 (not_16_out, D);
  and and_12 (and_12_out, B, not_17_out);
  not not_17 (not_17_out, C);
  and and_13 (and_13_out, B, not_18_out);
  not not_18 (not_18_out, D);
  not not_19 (not_19_out, B);
  and and_14 (and_14_out, not_19_out, C);
  and and_15 (and_15_out, B, not_20_out);
  not not_20 (not_20_out, C);
  and and_16 (and_16_out, B, not_21_out);
  not not_21 (not_21_out, D);
  or or_2 (a_2, and_1_out, C, and_2_out, A);
  or or_3 (b_2, not_3_out, and_3_out, and_4_out);
  or or_4 (d_2, and_5_out, and_6_out, and_7_out, and_8_out, A);
  or or_5 (e, and_9_out, and_10_out);
  or or_6 (f, and_11_out, and_12_out, and_13_out, A);
  or or_7 (g, and_14_out, and_15_out, and_16_out, A);
endmodule

module select (
  input  [3:0] in_1,
  input  [3:0] in_2,
  input  [3:0] in_3,
  input  [3:0] in_4,
  input  [1:0] in_5,
  input  [1:0] in_6,
  input  in_7,
  output [3:0] out_8,
  output [3:0] out_9,
  output out_10
);

  Multiplexer #(.select(2), .width(4)) multiplexer_1 (
    .in0(in_1), .in1(in_2), .in2(in_3), .in3(in_4), .out(out_8), .sel(in_5));  // open: en
  Multiplexer #(.select(2), .width(4)) multiplexer_2 (
    .in0(in_1), .in1(in_2), .in2(in_3), .in3(in_4), .out(out_9), .sel(in_6));  // open: en
  Multiplexer multiplexer_3 (.in0(1'b0), .in1(1'b1), .out(out_10), .sel(in_7));  // open: en

  // Notes on the sheet:
  //   7 entradas
  //   Todos MUX conectados = A + A
endmodule

module displayTwo (
  input  A,
  input  B,
  input  C,
  input  D,
  output a_2,
  output b_2,
  output c_2,
  output d_2,
  output e,
  output f,
  output g,
  output ponto
);

  wire and_1_out, and_2_out, and_3_out, and_4_out, and_5_out, and_6_out, and_7_out, and_8_out, and_9_out,
       and_10_out, and_11_out, and_12_out, and_13_out, and_14_out, and_15_out, and_16_out, and_17_out,
       and_18_out, and_19_out, and_20_out, and_21_out, and_22_out, and_23_out, and_24_out, and_25_out,
       and_26_out, and_27_out, and_28_out, not_1_out, not_2_out, not_3_out, not_4_out, not_5_out, not_6_out,
       not_7_out, not_8_out, not_9_out, not_10_out, not_11_out, not_12_out, not_13_out, not_14_out,
       not_15_out, not_16_out, not_17_out, not_18_out, not_19_out, not_20_out, not_21_out, not_22_out,
       not_23_out, not_24_out, not_25_out, not_26_out, not_27_out, not_28_out, not_29_out, not_30_out,
       not_31_out, not_32_out, not_33_out, not_34_out, not_35_out, not_36_out, not_37_out, not_38_out,
       not_39_out, not_40_out, not_41_out, not_42_out, not_43_out, not_44_out, not_45_out, not_46_out,
       not_47_out, not_48_out, not_49_out, not_50_out, not_51_out, not_52_out;

  not not_1 (not_1_out, A);
  and and_1 (and_1_out, not_1_out, not_2_out, not_3_out);
  not not_2 (not_2_out, B);
  not not_3 (not_3_out, D);
  not not_4 (not_4_out, A);
  and and_2 (and_2_out, not_4_out, C);
  not not_5 (not_5_out, A);
  and and_3 (and_3_out, not_5_out, B, D);
  not not_6 (not_6_out, B);
  and and_4 (and_4_out, A, not_6_out, not_7_out);
  not not_7 (not_7_out, C);
  not not_8 (not_8_out, A);
  and and_5 (and_5_out, not_8_out, not_9_out);
  not not_9 (not_9_out, B);
  not not_10 (not_10_out, A);
  and and_6 (and_6_out, not_10_out, not_11_out, not_12_out);
  not not_11 (not_11_out, C);
  not not_12 (not_12_out, D);
  not not_13 (not_13_out, B);
  and and_7 (and_7_out, not_13_out, not_14_out);
  not not_14 (not_14_out, C);
  not not_15 (not_15_out, A);
  and and_8 (and_8_out, not_15_out, C, D);
  not not_16 (not_16_out, B);
  and and_9 (and_9_out, not_16_out, not_17_out);
  not not_17 (not_17_out, C);
  not not_18 (not_18_out, A);
  and and_10 (and_10_out, not_18_out, D);
  not not_19 (not_19_out, A);
  and and_11 (and_11_out, not_19_out, B);
  not not_20 (not_20_out, A);
  not not_21 (not_21_out, B);
  not not_22 (not_22_out, D);
  not not_23 (not_23_out, A);
  not not_24 (not_24_out, B);
  not not_25 (not_25_out, A);
  not not_26 (not_26_out, D);
  not not_27 (not_27_out, A);
  not not_28 (not_28_out, C);
  not not_29 (not_29_out, B);
  not not_30 (not_30_out, C);
  not not_31 (not_31_out, B);
  not not_32 (not_32_out, C);
  and and_12 (and_12_out, not_31_out, not_32_out, not_33_out);
  not not_33 (not_33_out, D);
  not not_34 (not_34_out, A);
  and and_13 (and_13_out, not_34_out, C, not_35_out);
  not not_35 (not_35_out, D);
  not not_36 (not_36_out, A);
  not not_37 (not_37_out, C);
  and and_14 (and_14_out, not_36_out, not_37_out, not_38_out);
  not not_38 (not_38_out, D);
  not not_39 (not_39_out, A);
  and and_15 (and_15_out, not_39_out, B, not_40_out);
  not not_40 (not_40_out, C);
  not not_41 (not_41_out, A);
  and and_16 (and_16_out, not_41_out, B, not_42_out);
  not not_42 (not_42_out, D);
  and and_17 (and_17_out, A, not_43_out, not_44_out);
  not not_43 (not_43_out, B);
  not not_44 (not_44_out, C);
  not not_45 (not_45_out, A);
  and and_18 (and_18_out, not_45_out, not_46_out, C);
  not not_46 (not_46_out, B);
  not not_47 (not_47_out, A);
  and and_19 (and_19_out, not_47_out, B, not_48_out);
  not not_48 (not_48_out, C);
  not not_49 (not_49_out, A);
  and and_20 (and_20_out, not_49_out, B, not_50_out);
  not not_50 (not_50_out, D);
  and and_21 (and_21_out, A, not_51_out, not_52_out);
  not not_51 (not_51_out, B);
  not not_52 (not_52_out, C);
  and and_22 (and_22_out, A, C);
  and and_23 (and_23_out, A, B);
  or or_1 (a_2, and_1_out, and_2_out, and_3_out, and_4_out);
  or or_2 (b_2, and_5_out, and_6_out, and_7_out, and_8_out);
  or or_3 (c_2, and_9_out, and_10_out, and_11_out);
  and and_24 (and_24_out, not_20_out, not_21_out, not_22_out);
  and and_25 (and_25_out, not_23_out, not_24_out, C);
  and and_26 (and_26_out, not_25_out, C, not_26_out);
  and and_27 (and_27_out, not_27_out, B, not_28_out, D);
  and and_28 (and_28_out, A, not_29_out, not_30_out);
  or or_4 (e, and_12_out, and_13_out);
  or or_5 (f, and_14_out, and_15_out, and_16_out, and_17_out);
  or or_6 (g, and_18_out, and_19_out, and_20_out, and_21_out);
  or or_7 (ponto, and_22_out, and_23_out);
  or or_8 (d_2, and_24_out, and_25_out, and_26_out, and_27_out, and_28_out);
endmodule

module sumPart1 (
  input  Cin,
  input  A,
  input  B,
  output SUm,
  output Cout
);

  wire and_1_out, and_2_out, xor_1_out;

  xor xor_1 (xor_1_out, A, B);
  xor xor_2 (SUm, xor_1_out, Cin);
  and and_1 (and_1_out, Cin, xor_1_out);
  and and_2 (and_2_out, B, A);
  or or_1 (Cout, and_1_out, and_2_out);
endmodule

module sumComplet (
  input  [3:0] A,
  input  [3:0] B,
  output [3:0] out_3,
  output out_4
);

  wire sumpart1_1_cout, sumpart1_2_cout, sumpart1_3_cout;

  sumPart1 sumpart1_1 (.Cin(A[0]), .A(B[0]), .B(1'b0), .SUm(out_3[0]), .Cout(sumpart1_1_cout));
  sumPart1 sumpart1_2 (.Cin(A[1]), .A(B[1]), .B(sumpart1_1_cout), .SUm(out_3[1]), .Cout(sumpart1_2_cout));
  sumPart1 sumpart1_3 (.Cin(A[2]), .A(B[2]), .B(sumpart1_2_cout), .SUm(out_3[2]), .Cout(sumpart1_3_cout));
  sumPart1 sumpart1_4 (.Cin(A[3]), .A(B[3]), .B(sumpart1_3_cout), .SUm(out_3[3]), .Cout(out_4));
endmodule

module subtracao (
  input  A,
  input  B,
  input  Bin,
  output diferenca,
  output Bout
);

  wire and_1_out, and_2_out, and_3_out, and_4_out, and_5_out, and_6_out, and_7_out, not_1_out, not_2_out,
       not_3_out, not_4_out, not_5_out, not_6_out, not_7_out, not_8_out;

  not not_1 (not_1_out, A);
  not not_2 (not_2_out, B);
  not not_3 (not_3_out, A);
  not not_4 (not_4_out, Bin);
  not not_5 (not_5_out, B);
  not not_6 (not_6_out, Bin);
  not not_7 (not_7_out, A);
  not not_8 (not_8_out, A);
  and and_1 (and_1_out, not_1_out, not_2_out, Bin);
  and and_2 (and_2_out, not_3_out, B, not_4_out);
  and and_3 (and_3_out, A, not_5_out, not_6_out);
  and and_4 (and_4_out, A, B, Bin);
  and and_5 (and_5_out, not_7_out, Bin);
  and and_6 (and_6_out, not_8_out, B);
  and and_7 (and_7_out, B, Bin);
  or or_1 (diferenca, and_1_out, and_2_out, and_3_out, and_4_out);
  or or_2 (Bout, and_5_out, and_6_out, and_7_out);
endmodule

module subtracaoComplet (
  input  [3:0] A,
  input  [3:0] B,
  output [3:0] Out,
  output OVERFLOW
);

  wire subtracao_1_bout, subtracao_2_bout, subtracao_3_bout;

  subtracao subtracao_1 (.A(A[0]), .B(B[0]), .Bin(1'b0), .diferenca(Out[0]), .Bout(subtracao_1_bout));
  subtracao subtracao_2 (.A(A[1]), .B(B[1]), .Bin(subtracao_1_bout), .diferenca(Out[1]), .Bout(subtracao_2_bout));
  subtracao subtracao_3 (.A(A[2]), .B(B[2]), .Bin(subtracao_2_bout), .diferenca(Out[2]), .Bout(subtracao_3_bout));
  subtracao subtracao_4 (.A(A[3]), .B(B[3]), .Bin(subtracao_3_bout), .diferenca(Out[3]), .Bout(OVERFLOW));
endmodule

module select2two (
  input  [3:0] A,
  input  [3:0] B,
  input  in_3,
  output [3:0] OUT,
  output out_5
);

  wire and_1_out, and_2_out, and_3_out, not_1_out, subtracaocomplet_1_overflow, sumcomplet_1_out_4;
  wire [3:0] demultiplexer_1_out0, demultiplexer_1_out1, multiplexer_1_out, negator_1_out,
       subtracaocomplet_1_out, sumcomplet_1_out_3;

  sumComplet sumcomplet_1 (.A(A), .B(B), .out_3(sumcomplet_1_out_3), .out_4(sumcomplet_1_out_4));
  subtracaoComplet subtracaocomplet_1 (
    .A(A), .B(B), .Out(subtracaocomplet_1_out), .OVERFLOW(subtracaocomplet_1_overflow));
  not not_1 (not_1_out, in_3);
  Multiplexer #(.width(4)) multiplexer_1 (
    .in0(sumcomplet_1_out_3), .in1(subtracaocomplet_1_out), .out(multiplexer_1_out), .sel(in_3));  // open: en
  and and_1 (and_1_out, sumcomplet_1_out_4, not_1_out);
  and and_2 (and_2_out, subtracaocomplet_1_overflow, in_3);
  or or_1 (out_5, and_1_out, and_2_out);
  and and_3 (and_3_out, out_5, in_3);
  Demultiplexer #(.width(4)) demultiplexer_1 (
    .out0(demultiplexer_1_out0), .out1(demultiplexer_1_out1), .in(multiplexer_1_out), .sel(and_3_out));  // open: en
  Negator #(.width(4)) negator_1 (.in(demultiplexer_1_out1), .out(negator_1_out));
  Multiplexer #(.width(4)) multiplexer_2 (
    .in0(demultiplexer_1_out0), .in1(negator_1_out), .out(OUT), .sel(and_3_out));  // open: en
endmodule

module FINAL (
  input  [3:0] A,
  input  [3:0] B,
  input  [3:0] C,
  input  [3:0] D,
  input  [1:0] ENTRADA_1,
  input  [1:0] ENTRADA_2,
  input  Operacao
);

  wire displaytwo_1_a_2, displaytwo_1_b_2, displaytwo_1_c_2, displaytwo_1_d_2, displaytwo_1_e,
       displaytwo_1_f, displaytwo_1_g, displaytwo_1_ponto, select2two_1_out_5, select_1_out_10;
  wire [3:0] select2two_1_out, select_1_out_8, select_1_out_9;

  select select_1 (
    .in_1(A), .in_2(B), .in_3(C), .in_4(D), .in_5(ENTRADA_1), .in_6(ENTRADA_2), .in_7(Operacao),
    .out_8(select_1_out_8), .out_9(select_1_out_9), .out_10(select_1_out_10));
  select2two select2two_1 (
    .A(select_1_out_8), .B(select_1_out_9), .in_3(select_1_out_10), .OUT(select2two_1_out),
    .out_5(select2two_1_out_5));
  LED led_1 (.in(select2two_1_out_5));
  displayTwo displaytwo_1 (
    .A(select2two_1_out[3]), .B(select2two_1_out[2]), .C(select2two_1_out[1]), .D(select2two_1_out[0]),
    .a_2(displaytwo_1_a_2), .b_2(displaytwo_1_b_2), .c_2(displaytwo_1_c_2), .d_2(displaytwo_1_d_2),
    .e(displaytwo_1_e), .f(displaytwo_1_f), .g(displaytwo_1_g), .ponto(displaytwo_1_ponto));
  _7_Segment_Display u_7_segment_display_1 (
    .g(displaytwo_1_g), .f(displaytwo_1_f), .a(displaytwo_1_a_2), .b(displaytwo_1_b_2), .e(displaytwo_1_e),
    .d(displaytwo_1_d_2), .c(displaytwo_1_c_2), .dp(displaytwo_1_ponto));

  // Notes on the sheet:
  //   Trabalho Final 
  //   SOMA = 0
  //   SUBTRACAO = 1
  //   00 = A
  //   01 = B
  //   10 = C
  //   11 = D
  //   out 1
  //   out 2
  //   se Operacao = 0, Led = "16 + display"
  //   se Operacao = 1, Led = "-display"
  //   " . " = número > 10
endmodule
